# Fritzing sketch martes2 (saved by Fritzing 0.9.1b)
breadboards: 1

parts:
  Part1 = Arduino Uno (Rev3)
  S1 = Pushbutton [package="[THT]"]

nets:
  N1: Part1.D12/MISO, S1.Pin_3, S1.Pin_4
  N2: Part1.GND, S1.Pin_1, S1.Pin_2
