# Fritzing sketch miercoles1_3 (saved by Fritzing 0.9.1b)

parts:
  Q1 = LTR-301 [package=ltr-301]
  LED1 = LED - 5mm [color="Infrared (940nm)" package="5 mm [THT]"]  # not connected
  R1 = Resistor [tolerance=±5% resistance=470 package=THT]
  R2 = Resistor [tolerance=±5% resistance=10k package=THT]

nets:
  Arduino: Q1.C, R2.Pin_1
  GND: Q1.E
  5V: R1.Pin_0, R2.Pin_0
